# Fritzing sketch sketch (saved by Fritzing 0.9.9b)
breadboards: 1

parts:
  Mod1 = KY-019 5V Relay Module [package="Breakout board"]
  Part1 = FC-28 Soil Hygrometer Module
  Part2 = FC-28 Soil Hygrometer Module - Probe
  LED1 = LED - 5mm [color="Red (633nm)" current=0.030 package="5 mm [THT]"]
  LED2 = LED - 5mm [color="Yellow (595nm)" current=0.030 package="5 mm [THT]"]
  LED3 = LED - 5mm [color="Green (570nm)" current=0.030 package="5 mm [THT]"]
  R1 = Resistor [tolerance=±5% power=0.25 resistance=220 package=THT]
  R2 = Resistor [tolerance=±5% power=0.25 resistance=220 package=THT]
  R3 = Resistor [tolerance=±5% power=0.25 resistance=220 package=THT]
  Power_plug1 = Power plug
  M1 = DC Motor
  Part3 = Arduino Uno (Rev3)
  DHT1 = DHT11 Humitidy and Temperature Sensor (3 pins)

nets:
  N1: Mod1.S, Part3.D8
  VCC: Mod1.+, Part1.VCC, Part3.5V, DHT1.Plus
  GND: Mod1.-, Part1.GND, LED1.cathode, LED2.cathode, LED3.cathode, Part3.GND, DHT1.Gnd
  N2: Mod1.Common, Power_plug1.VCC
  N3: Mod1.NO, M1.pin_1
  N4: Part1.DO, Part3.D7
  N5: Part1.AO, Part3.A0
  N6: Part1.POS, Part2.POS
  N7: Part1.NEG, Part2.NEG
  N8: LED1.anode, R2.Pin_0
  N9: LED2.anode, R1.Pin_1
  N10: LED3.anode, R3.Pin_0
  N11: R1.Pin_0, Part3.D3_PWM
  N12: R2.Pin_1, Part3.D2
  N13: R3.Pin_1, Part3.D4
  N14: Power_plug1.GND, M1.pin_2
  N15: Part3.D12/MISO, DHT1.Signal

custom parts:
  KY-019 5V Relay Module: KY-019 5V Relay module, used to control AC circuits. (Special thanks to vanepp for fixing the PCB holes and other errors)
  FC-28 Soil Hygrometer Module: The FC-28 is a soil hygrometer module that uses the Texas Instruments LM393 comparator chip to provide an analog measurement of soil humidity. The digital output is high when soil moisture is over a certain threshold, as determined by adjusting the potentiometer.
  FC-28 Soil Hygrometer Module - Probe: The FC-28 is a soil hygrometer module that uses the Texas Instruments LM393 comparator chip to provide an analog measurement of soil humidity.
  DHT11 Humitidy and Temperature Sensor (3 pins): DHT11 Humidity and Temperature Sensor (3 pins).

// code stored in the sketch: sketch.ino
#include <ESP8266Wifi.h>
#include <WiFiClient.h>


using namespace std;


// Wifi
const char* ssid = "THREE O'CLOCK FREEWIFI";
const char* password = "";


// Led
int red_led = 2;
int yellow_led = 3;
int green_led = 4;


// Soil moisture sensor
int soil_d_pin = 7;
int soil_a_pin = A0;


// Moisture level
int low_moisture = 300;
int high_moisture = 700;


// CONNECTING
void connect_wifi() {
  WiFI.begin(ssid, password);
  while (WiFi.status() != WL_CONNECTED)
  {
    delay(500);
    Serial.println(".");
  }


  Serial.println();
  Serial.print("Connected to Wifi: ");
  Serial.println(ssid);
  Serial.print("IP Address: ");
  Serial.println(WiFi.localIP());
}


void connect_led() {
  pinMode(red_led, OUTPUT);
  pinMode(yellow_led, OUTPUT);
  pinMode(green_led, OUTPUT);
}


void connect_soil_moisture_sensor() {
  pinMode(soil_d_pin, OUTPUT);
  digitalWrite(soil_d_pin, LOW);
}


// SOMETHING
void turn_on_led(int led) {
  for (int i = 2; i <= 4; i++)
    digitalWrite(i, LOW);
  
  // led = 0 --> red
  // led = 1 --> yellow
  // led = 2 --> green
  digitalWrite(led + 2, HIGH);
}


double measure_soil_moisture() {
  digitalWrite(soil_d_pin, HIGH);
  delay(10);


  int moisture_value = analogRead(soil_a_pin);
  int moisture_percent = map(moisture_value, 0, 1023, 0, 100);


  if(moisture_value <= low_moisture) {
    turn_on_led(0);
  }
  else if(moisture_value >= high_moisture) {
    turn_on_led(2);
  }
  else {
    turn_on_led(1);
  }


  return moisture_percent;


}


// SET UP & RUN
void setup() {
  Serial.begin(9600);
  // WIFI
  //connect_wifi();


  // LED
  connect_led();


  // Soil moisture sensor
  connect_soil_moisture_sensor()
}


void loop()
{


}
